// Logisim project Circuito alarme projeto 2.circ as structural Verilog: 1 circuit, main circuit main
module main (
  input  A,
  input  B,
  input  C,
  output S
);

  wire and_1_out, and_2_out;

  and and_1 (and_1_out, A, C);
  and and_2 (and_2_out, B, C);
  or or_1 (S, and_1_out, and_2_out);

  // Notes on the sheet:
  //   AC + BC
endmodule
